# Fritzing sketch splate_v1 (saved by Fritzing 0.9.3b)

parts:
  Часть1 = Arduino Uno (Rev3)
  S1 = H-Bridge with L298N
  M1 = DC Motor
  M2 = DC Motor
  BAT1 = 18650 battery holder [package=battery-18650-kit]
  BAT2 = 18650 battery holder [package=battery-18650-kit]  # not connected
  Raspberry_Pi1 = Raspberry Pi B+  # not connected
  M3 = RioRand LM2596  # not connected
  BAT3 = 18650 battery holder [package=battery-18650-kit]  # not connected
  BAT4 = 18650 battery holder [package=battery-18650-kit]  # not connected
  BAT5 = 18650 battery holder [package=battery-18650-kit]  # not connected
  BAT6 = 18650 battery holder [package=battery-18650-kit]  # not connected
  BAT7 = 18650 battery holder [package=battery-18650-kit]  # not connected
  U2 = SWITCH_SPDT [package=kps-1290]

nets:
  N1: Часть1.D3_PWM, S1.ENB
  N2: Часть1.D4, S1.IN4
  N3: Часть1.D5_PWM, S1.IN3
  N4: Часть1.D6_PWM, S1.IN2
  N5: Часть1.D7, S1.IN1
  N6: S1.12V, U2.S
  N7: S1.M1-01, M1.pin_2
  N8: S1.M1-02, M1.pin_1
  N9: S1.M2-01, M2.pin_2
  N10: S1.M2-02, M2.pin_1
  N11: BAT1.+, U2.O

custom parts:
  H-Bridge with L298N: h-bridge
  18650 battery holder: 18650 Battery Holder
